# Fritzing sketch single PCB (saved by Fritzing 0.9.3b)
circuit board: 7cm x 6cm
breadboards: 1

parts:
  ATMEGA328-M1 = atmega328 [package=dip]
  MULTIPLEXER = Analog Digital MUX Breakout
  16MHz = Crystal [frequency="16 Mhz" package=THT]
  22pF = Ceramic Capacitor [capacitance=10pF voltage=10V package="100 mil [THT, multilayer]"]
  PEG_BOARD_CONNECTOR1 = molex pin header, 10 pins [form=molex]
  M_START = Pushbutton [package="[THT]"]
  RESET = Pushbutton [package="[THT]"]
  R1 = Resistor [tolerance=±1% resistance=10k package="1206 [SMD]"]
  R2 = Resistor [tolerance=±1% resistance=10k package="1206 [SMD]"]
  R3 = Resistor [tolerance=±1% resistance=10k package="1206 [SMD]"]
  R4 = Resistor [tolerance=±1% resistance=10k package="1206 [SMD]"]
  R5 = Resistor [tolerance=±1% resistance=10k package="1206 [SMD]"]
  R6 = Resistor [tolerance=±1% resistance=10k package="1206 [SMD]"]
  R8 = Resistor [tolerance=±1% resistance=10k package="1206 [SMD]"]
  R9 = Resistor [tolerance=±1% resistance=10k package="1206 [SMD]"]
  R10 = Resistor [tolerance=±1% resistance=10k package="1206 [SMD]"]
  ADLED = molex pin header, 3 pins [form=molex]
  DC_9V_JACK = Power plug
  BT = LED - 3mm [color="Blue (525nm)" package="3 mm [THT]"]
  7805-LED = Voltage Regulator - 5V [package="TO220 [THT]"]
  7805-WELL = Voltage Regulator - 5V [package="TO220 [THT]"]
  7805-DIG = Voltage Regulator - 5V [package="TO220 [THT]"]
  Buzzer = Buzzer 12mm [package=buzzer-12mm-ns-kit]
  Pot_Div = Resistor [tolerance=±5% resistance=1M package=THT]
  R11 = Resistor [tolerance=±5% resistance=1M package=THT]
  R13 = Resistor [tolerance=±5% resistance=1M package=THT]
  R14 = Resistor [tolerance=±5% resistance=1M package=THT]
  22pF_2 = Ceramic Capacitor [capacitance=100nF package="100 mil [THT, multilayer]"]
  R15 = Resistor [tolerance=±5% resistance=10k package="1206 [SMD]"]
  470uF = Electrolytic Capacitor [capacitance=1µF voltage=20V package="200 mil [THT, electrolytic]"]
  BAT = female pin header, 2 pins [form="♀ (female)"]
  R16 = Resistor [tolerance=±5% resistance=10k package="1206 [SMD]"]
  Diode = Rectifier Diode [part_number=1N4001 package="300 mil [THT]"]
  CRG = LED - 3mm [color="Red (633nm)" package="3 mm [THT]"]
  R17 = Resistor [tolerance=±5% resistance=10k package="1206 [SMD]"]
  330 = Resistor [tolerance=±5% resistance=330 package=THT]
  SWT = female pin header, 2 pins [form="♀ (female)"]
  10uF = Electrolytic Capacitor [capacitance=10µF voltage=20V package="100 mil [THT, electrolytic]"]
  PWR = LED - 3mm [color="Green (565nm)" package="3 mm [THT]"]
  10uF_2 = Electrolytic Capacitor [capacitance=10µF voltage=20V package="100 mil [THT, electrolytic]"]
  1K = Resistor [tolerance=±5% resistance=220 package=THT]
  1K_2 = Resistor [tolerance=±5% resistance=220 package=THT]
  10uF_3 = Electrolytic Capacitor [capacitance=10µF voltage=20V package="100 mil [THT, electrolytic]"]

nets:
  N1: ATMEGA328-M1.RESET, RESET.Pin_3, RESET.Pin_4, R15.Pin_1
  N2: ATMEGA328-M1.D2, M_START.Pin_1, M_START.Pin_2, R16.Pin_1
  +5VCC(DIG): ATMEGA328-M1.VCC, ATMEGA328-M1.AVCC, MULTIPLEXER.VCC, M_START.Pin_3, M_START.Pin_4, 7805-DIG.output_voltage, R15.Pin_0, 10uF.+
  gnd: ATMEGA328-M1.GND, MULTIPLEXER.GND, MULTIPLEXER.EN, 22pF.0, RESET.Pin_2, R1.Pin_0, R2.Pin_0, R3.Pin_0, R4.Pin_0, R5.Pin_0, R6.Pin_0, R8.Pin_0, R9.Pin_0, R10.Pin_0, ADLED.pin3, DC_9V_JACK.GND, BT.cathode, 7805-LED.GND, 7805-WELL.GND, 7805-DIG.GND, Buzzer.2, R11.Pin_0, 22pF_2.0, 470uF.-, BAT.pin2, R16.Pin_0, R17.Pin_0, 10uF.-, PWR.cathode, 10uF_2.-, 10uF_3.-
  N3: ATMEGA328-M1.XLAT1, 16MHz.pin_0, 22pF_2.1
  N4: ATMEGA328-M1.XLAT2, 16MHz.pin_1, 22pF.1
  N5: ATMEGA328-M1.D5_(PWM), Buzzer.1
  N6: ATMEGA328-M1.D6_(PWM), 330.Pin_1
  N7: ATMEGA328-M1.D7, 1K_2.Pin_0
  N8: ATMEGA328-M1.D8, 1K.Pin_0
  N9: ATMEGA328-M1.D9_(PWM), MULTIPLEXER.S0
  N10: ATMEGA328-M1.D10_(PWM), MULTIPLEXER.S1
  N11: ATMEGA328-M1.D11_(PWM), MULTIPLEXER.S2
  N12: ATMEGA328-M1.D12, MULTIPLEXER.S3
  N13: ATMEGA328-M1.A0, MULTIPLEXER.SIG
  B POT DIV: ATMEGA328-M1.A1, Pot_Div.Pin_1, R14.Pin_1
  N14: MULTIPLEXER.C0, PEG_BOARD_CONNECTOR1.pin10, R1.Pin_1
  N15: MULTIPLEXER.C1, PEG_BOARD_CONNECTOR1.pin9, R2.Pin_1
  N16: MULTIPLEXER.C2, PEG_BOARD_CONNECTOR1.pin8, R3.Pin_1
  N17: MULTIPLEXER.C3, PEG_BOARD_CONNECTOR1.pin7, R4.Pin_1
  N18: MULTIPLEXER.C4, PEG_BOARD_CONNECTOR1.pin6, R5.Pin_1
  N19: MULTIPLEXER.C5, PEG_BOARD_CONNECTOR1.pin5, R6.Pin_1
  N20: MULTIPLEXER.C6, PEG_BOARD_CONNECTOR1.pin4, R8.Pin_1
  N21: MULTIPLEXER.C7, PEG_BOARD_CONNECTOR1.pin3, R9.Pin_1
  N22: MULTIPLEXER.C8, PEG_BOARD_CONNECTOR1.pin2, R10.Pin_1
  +5VCC(WELL): PEG_BOARD_CONNECTOR1.pin1, 7805-WELL.output_voltage, 10uF_3.+
  +5VCC(LED): ADLED.pin1, 7805-LED.output_voltage, 10uF_2.+
  DIN: ADLED.pin2, 330.Pin_0
  N23: DC_9V_JACK.VCC, Diode.anode, CRG.anode
  N24: BT.anode, 1K_2.Pin_1
  +Vbat: 7805-LED.input_voltage, 7805-WELL.input_voltage, 7805-DIG.input_voltage, R13.Pin_0, 470uF.+, SWT.pin2
  N25: Pot_Div.Pin_0, R11.Pin_1
  N26: R13.Pin_1, R14.Pin_0
  N27: BAT.pin1, Diode.cathode, SWT.pin1
  N28: CRG.cathode, R17.Pin_1
  N29: PWR.anode, 1K.Pin_1

notes:
  CMC | COHMET-V1.0
  18012001|06092000
  -----------------------------------------------------------------
  ---------------------------------------------------------
  + - n 9 8 7 6 5 4 3 2 1
  -GND
  + - D
  +VCC
  - +
  K V G T R S
  V G T R
  + 9 8 7 6 5 4 3 2 1
  + D -
  + -
  -------Made in INDIA-------
  Designed & Developed
  in INDIA
  8/8/2025
  ---Designed & Developed---
  Cassandra | Suraksha | Shreenandan
  COHMET V1, COgnition and Hand Motor skills Enhancement Trainer, 2.0
  Stable COHMET PCB
